// Logisim project cpu_design.circ as structural Verilog: 9 circuits, main circuit main
module main (
  input  [2:0] in_1,
  input  in_2,
  input  in_3
);

  wire CLK, or_1_out, undriven, undriven_2, undriven_3, undriven_4, undriven_5, undriven_6;
  wire [2:0] priority_encoder_1_out;
  wire [3:0] bit_extender_1_out;
  wire [7:0] alu_final_1_output, rom_1_data, undriven_7, undriven_8;

  Clock clock_1 (.out(CLK));
  ROM #(.addrWidth(4)) rom_1 (.data(rom_1_data));  // open: addr, sel
  or or_1 (or_1_out, undriven, undriven_2, undriven_3, undriven_4, undriven_5, undriven_6);
  Priority_Encoder priority_encoder_1 (
    .in0(undriven), .in1(undriven_2), .in2(undriven_3), .in3(undriven_4), .in4(undriven_5), .in5(undriven_6),
    .out(priority_encoder_1_out), .en_in(in_3), .gs(in_2));  // open: in6, in7, en_out
  assign bit_extender_1_out = {{1{1'b0}}, priority_encoder_1_out};  // Bit_Extender bit_extender_1
  ALU_Final alu_final_1 (
    .Opcode(bit_extender_1_out), .input_a(undriven_7), .input_b(undriven_8), .\output (alu_final_1_output));  // open: carry_out, z_flag, overflow_flag
  Register register_1 (.D(alu_final_1_output), .clk(CLK));  // open: en, Q, clr
endmodule

// au
module AU (
  input  [7:0] input_b,
  input  [7:0] input_a,
  input  mode_sub_add,
  output C_OUT,
  output [7:0] \output ,
  output z_flag,
  output overflow_flag
);

  wire xnor_1_out, xor_2_out;
  wire [7:0] bit_extender_1_out, xor_1_out;

  assign bit_extender_1_out = {{7{mode_sub_add}}, mode_sub_add};  // Bit_Extender bit_extender_1
  assign xor_1_out = input_b ^ bit_extender_1_out;  // XOR_Gate xor_1, 8 bits wide
  xor xor_2 (xor_2_out, \output [7], input_b[7]);
  xnor xnor_1 (xnor_1_out, input_b[7], input_a[7]);
  Adder adder_1 (.a(input_a), .b(xor_1_out), .out(\output ), .cin(mode_sub_add), .cout(C_OUT));
  and and_1 (overflow_flag, xor_2_out, xnor_1_out);
  Comparator comparator_1 (.a(\output ), .b({8{1'b0}}), .eq(z_flag));  // open: gt, lt
endmodule

module LU (
  input  [7:0] input_a,
  input  [7:0] input_b,
  input  _1,
  input  _2,
  output [7:0] \output 
);

  wire [7:0] and_1_out, not_1_out, or_1_out, xor_1_out;

  assign xor_1_out = input_a ^ input_b;  // XOR_Gate xor_1, 8 bits wide
  assign or_1_out = input_a | input_b;  // OR_Gate or_1, 8 bits wide
  assign and_1_out = input_a & input_b;  // AND_Gate and_1, 8 bits wide
  assign not_1_out = ~input_a;  // NOT_Gate not_1, 8 bits wide
  Multiplexer #(.select(2), .width(8), .enable("false")) multiplexer_1 (
    .in0(xor_1_out), .in1(or_1_out), .in2(and_1_out), .in3(not_1_out), .out(\output ), .sel({_1, _2}));
endmodule

// ALU
module ALU_Final (
  input  [3:0] Opcode,
  input  [7:0] input_a,
  input  [7:0] input_b,
  output carry_out,
  output [7:0] \output ,
  output z_flag,
  output overflow_flag
);

  wire [7:0] arthmetic_unit_output, logic_unit_output, multiplexer_1_out, multiplexer_2_out, not_1_out,
       not_2_out;

  assign not_1_out = ~input_a;  // NOT_Gate not_1, 8 bits wide
  assign not_2_out = ~input_b;  // NOT_Gate not_2, 8 bits wide
  Multiplexer #(.width(8)) multiplexer_1 (
    .in0(input_a), .in1(not_1_out), .out(multiplexer_1_out), .sel(Opcode[0]));  // open: en
  Multiplexer #(.width(8)) multiplexer_2 (
    .in0(input_b), .in1(not_2_out), .out(multiplexer_2_out), .sel(Opcode[1]));  // open: en
  AU arthmetic_unit (
    .input_b(multiplexer_2_out), .input_a(multiplexer_1_out), .mode_sub_add(Opcode[2]), .C_OUT(carry_out),
    .\output (arthmetic_unit_output), .z_flag(z_flag), .overflow_flag(overflow_flag));
  LU logic_unit (
    .input_a(input_a), .input_b(multiplexer_2_out), ._1(Opcode[2]), ._2(Opcode[0]),
    .\output (logic_unit_output));
  Multiplexer #(.width(8)) multiplexer_3 (
    .in0(arthmetic_unit_output), .in1(logic_unit_output), .out(\output ), .sel(Opcode[3]));  // open: en

  // Other names for the same wires on the sheet: f0 = Opcode[0]; f1 = Opcode[1]; f2 = Opcode[2]; f3 = Opcode[3]
endmodule

// rig
module Register_File (
  input  [7:0] Data_in,
  input  enable_write,
  input  CLK,
  input  [1:0] read_addr_a,
  input  [1:0] write_addr,
  input  [1:0] read_addr_b,
  input  reset,
  output [7:0] Value_a,
  output [7:0] value_b
);

  wire demultiplexer_1_out0, demultiplexer_1_out1, demultiplexer_1_out2, demultiplexer_1_out3;
  wire [3:0] register_1_q, register_1_q_2;
  wire [7:0] register_2_q, register_3_q, register_4_q;

  Demultiplexer #(.select(2)) demultiplexer_1 (
    .out0(demultiplexer_1_out0), .out1(demultiplexer_1_out1), .out2(demultiplexer_1_out2),
    .out3(demultiplexer_1_out3), .in(enable_write), .sel(write_addr));  // open: en
  Hex_Digit_Display hex_digit_display_1 (.value(register_1_q_2));  // open: dp
  Register register_1 (
    .D(Data_in), .en(demultiplexer_1_out0), .Q({register_1_q_2, register_1_q}), .clk(CLK), .clr(reset));
  Register register_2 (.D(Data_in), .en(demultiplexer_1_out1), .Q(register_2_q), .clk(CLK), .clr(reset));
  Register register_3 (.D(Data_in), .en(demultiplexer_1_out2), .Q(register_3_q), .clk(CLK), .clr(reset));
  Register register_4 (.D(Data_in), .en(demultiplexer_1_out3), .Q(register_4_q), .clk(CLK), .clr(reset));
  Hex_Digit_Display hex_digit_display_2 (.value(register_1_q));  // open: dp
  Multiplexer #(.select(2), .width(8)) multiplexer_1 (
    .in0({register_1_q_2, register_1_q}), .in1(register_2_q), .in2(register_3_q), .in3(register_4_q),
    .out(Value_a), .sel(read_addr_a));  // open: en
  Multiplexer #(.select(2), .width(8)) multiplexer_2 (
    .in0({register_1_q_2, register_1_q}), .in1(register_2_q), .in2(register_3_q), .in3(register_4_q),
    .out(value_b), .sel(read_addr_b));  // open: en

  // Notes on the sheet:
  //   rs1
  //   rs2
  //   rs3
  //   rs4
endmodule

module program_Counter (
  input  reset,
  output [3:0] out_2,
  output out_3
);

  Counter #(.width(4), .max('hf)) counter_1 (
    .count(1'b1), .Q(out_2), .clk(out_3), .clr(reset));  // open: load, D, carry
  Hex_Digit_Display hex_digit_display_1 (.value(out_2));  // open: dp
endmodule

module Mux_gates (
  input  [3:0] data_bus_in,
  input  f0,
  output [3:0] data_bus_out
);

  and and_1 (data_bus_out[0], data_bus_in[0], f0);
  and and_2 (data_bus_out[1], data_bus_in[1], f0);
  and and_3 (data_bus_out[2], data_bus_in[2], f0);
  and and_4 (data_bus_out[3], data_bus_in[3], f0);
  LED led_1 (.in(data_bus_out[0]));
  LED led_2 (.in(data_bus_out[1]));
  LED led_3 (.in(data_bus_out[2]));
  LED led_4 (.in(data_bus_out[3]));
endmodule

module demux_gates (
  input  [7:0] in_1,
  output [7:0] out_2,
  output out_3
);

  LED write_enable_status (.in(out_3));
  and and_1 (out_2[0], in_1[0], out_3);
  and and_2 (out_2[1], in_1[1], out_3);
  and and_3 (out_2[2], in_1[2], out_3);
  and and_4 (out_2[3], in_1[3], out_3);
  and and_5 (out_2[4], in_1[4], out_3);
  and and_6 (out_2[5], in_1[5], out_3);
  and and_7 (out_2[6], in_1[6], out_3);
  and and_8 (out_2[7], in_1[7], out_3);
endmodule

module mux (
  input  [7:0] addr_in,
  output [3:0] opcode
);

  wire [3:0] mux_gates_1_data_bus_out, mux_gates_2_data_bus_out, mux_gates_3_data_bus_out,
       mux_gates_4_data_bus_out, mux_gates_5_data_bus_out, mux_gates_6_data_bus_out,
       mux_gates_7_data_bus_out, mux_gates_8_data_bus_out;

  // NOT_Gate not_1 is placed but not wired
  Mux_gates mux_gates_1 (.data_bus_in(4'b0000), .f0(addr_in[0]), .data_bus_out(mux_gates_1_data_bus_out));
  Mux_gates mux_gates_2 (.data_bus_in(4'b0001), .f0(addr_in[1]), .data_bus_out(mux_gates_2_data_bus_out));
  Mux_gates mux_gates_3 (.data_bus_in(4'b1111), .f0(addr_in[2]), .data_bus_out(mux_gates_3_data_bus_out));
  Mux_gates mux_gates_4 (.data_bus_in(4'b1111), .f0(addr_in[3]), .data_bus_out(mux_gates_4_data_bus_out));
  Mux_gates mux_gates_5 (.data_bus_in(4'b1111), .f0(addr_in[4]), .data_bus_out(mux_gates_5_data_bus_out));
  Mux_gates mux_gates_6 (.data_bus_in(4'b1111), .f0(addr_in[5]), .data_bus_out(mux_gates_6_data_bus_out));
  Mux_gates mux_gates_7 (.data_bus_in(4'b1111), .f0(addr_in[6]), .data_bus_out(mux_gates_7_data_bus_out));
  Mux_gates mux_gates_8 (.data_bus_in(4'b1111), .f0(addr_in[7]), .data_bus_out(mux_gates_8_data_bus_out));
  assign opcode = mux_gates_1_data_bus_out | mux_gates_2_data_bus_out | mux_gates_3_data_bus_out | mux_gates_4_data_bus_out | mux_gates_5_data_bus_out | mux_gates_6_data_bus_out | mux_gates_7_data_bus_out | mux_gates_8_data_bus_out;  // OR_Gate or_1, 4 bits wide

  // Notes on the sheet:
  //   sub
  //   copy
  //   copy a
  //   load m
  //   load 2 m
  //   clear
  //   add
  //   not
endmodule
